// Logisim project brainfuck.circ as structural Verilog: 5 circuits, main circuit brainfuck/cpu
module main (
  input  in_1
);

  wire brainfuck_cpu_1_err, brainfuck_cpu_1_stdin_read, brainfuck_cpu_1_stdout_ready,
       brainfuck_cpu_1_writing_mem, clk, d_ff_1_q, d_ff_2_q, d_ff_3_q;
  wire [2:0] rom_1_data;
  wire [5:0] brainfuck_cpu_1_dbg_skip_stack_size, brainfuck_cpu_1_dbg_stack_length;
  wire [7:0] brainfuck_cpu_1_set_mem, brainfuck_cpu_1_stdout, multiplexer_1_out, ram_1_data, register_3_q,
       register_4_q, stdin_out_3, stdout_probe_output;
  wire [23:0] brainfuck_cpu_1_instr_ptr_2, brainfuck_cpu_1_mem_ptr_2, register_1_q, register_2_q;

  Clock clock_1 (.out(clk));
  // Probe on brainfuck_cpu_1_instr_ptr_2
  ROM #(.addrWidth(24), .dataWidth(3)) rom_1 (.addr(register_1_q), .data(rom_1_data));  // open: sel
  input_stream stdin (.clk(clk), .read(d_ff_1_q), .out_3(stdin_out_3));
  // Probe on brainfuck_cpu_1_mem_ptr_2
  // Probe on brainfuck_cpu_1_dbg_skip_stack_size
  LED led_1 (.in(brainfuck_cpu_1_err));
  // Probe on brainfuck_cpu_1_writing_mem
  // Probe on brainfuck_cpu_1_dbg_stack_length
  brainfuck_cpu brainfuck_cpu_1 (
    .instr(rom_1_data), .instr_ptr(register_1_q), .mem(multiplexer_1_out), .mem_ptr(register_2_q),
    .stdin(stdin_out_3), .instr_ptr_2(brainfuck_cpu_1_instr_ptr_2), .mem_ptr_2(brainfuck_cpu_1_mem_ptr_2),
    .writing_mem(brainfuck_cpu_1_writing_mem), .set_mem(brainfuck_cpu_1_set_mem),
    .stdout_ready(brainfuck_cpu_1_stdout_ready), .stdout(brainfuck_cpu_1_stdout),
    .stdin_read(brainfuck_cpu_1_stdin_read), .clk(clk), .err(brainfuck_cpu_1_err),
    .dbg_stack_length(brainfuck_cpu_1_dbg_stack_length),
    .dbg_skip_stack_size(brainfuck_cpu_1_dbg_skip_stack_size));
  // Probe on brainfuck_cpu_1_set_mem
  // Probe on brainfuck_cpu_1_stdout_ready
  // Probe on brainfuck_cpu_1_stdout
  // Probe on brainfuck_cpu_1_stdin_read
  Register #(.width(24)) register_1 (.D(brainfuck_cpu_1_instr_ptr_2), .Q(register_1_q), .clk(clk));  // open: en, clr
  D_Flip_Flop d_ff_1 (.clk(clk), .D(brainfuck_cpu_1_stdin_read), .Q(d_ff_1_q));  // open: Qn, preset, en, reset
  Register #(.width(24)) register_2 (.D(brainfuck_cpu_1_mem_ptr_2), .Q(register_2_q), .clk(clk));  // open: en, clr
  D_Flip_Flop d_ff_2 (.clk(clk), .D(brainfuck_cpu_1_writing_mem), .Q(d_ff_2_q));  // open: Qn, preset, en, reset
  Register register_3 (.D(brainfuck_cpu_1_set_mem), .Q(register_3_q), .clk(clk));  // open: en, clr
  D_Flip_Flop d_ff_3 (.clk(clk), .D(brainfuck_cpu_1_stdout_ready), .Q(d_ff_3_q));  // open: Qn, preset, en, reset
  Register register_4 (.D(brainfuck_cpu_1_stdout), .Q(register_4_q), .clk(clk));  // open: en, clr
  output_stream stdout (
    .clk(clk), .probing(in_1), .probe_addr({24{1'b0}}), .writing(d_ff_3_q), .value(register_4_q),
    .probe_output(stdout_probe_output));
  // Probe on stdout_probe_output
  // Probe on multiplexer_1_out
  RAM #(.addrWidth(24), .bus("separate")) ram_1 (
    .addr(register_2_q), .din(register_3_q), .data(ram_1_data), .str(d_ff_2_q), .clk(clk), .ld(1'b1));  // open: sel, clr
  Multiplexer #(.width(8)) multiplexer_1 (
    .in0(ram_1_data), .in1(register_3_q), .out(multiplexer_1_out), .sel(d_ff_2_q));  // open: en

  // Notes on the sheet:
  //   contents of rom_1 (hex, n*v repeats v):
  //   2 6 0 5 4 1 7
endmodule

// BF\nCPU
module brainfuck_cpu (
  input  clk,
  input  [2:0] instr,
  input  [23:0] instr_ptr,
  input  [7:0] mem,
  input  [23:0] mem_ptr,
  input  [7:0] stdin,
  output [23:0] instr_ptr_2,
  output [23:0] mem_ptr_2,
  output writing_mem,
  output [5:0] dbg_stack_length,
  output [7:0] set_mem,
  output stdout_ready,
  output [7:0] stdout,
  output stdin_read,
  output err,
  output [5:0] dbg_skip_stack_size
);

  wire and_1_out, and_2_out, and_3_out, and_4_out, and_5_out, and_6_out, and_7_out, comparator_1_eq,
       err_stack, input_minus, input_plus, input_t_t, input_t_t_t, input_t_t_t_t, input_t_t_t_t_t, or_1_out,
       or_2_out, or_3_out, or_4_out;
  wire [5:0] adder_1_out, bit_extender_1_out;
  wire [7:0] adder_3_out, bit_extender_3_out;
  wire [23:0] bit_extender_2_out, multiplexer_1_out, register24stack64_1_tail;

  and and_1 (and_1_out, instr[2], instr[1]);
  and and_2 (and_2_out, input_t_t_t_t, or_4_out);
  and and_3 (and_3_out, ~or_4_out, input_t_t_t_t_t);  // AND_Gate
  and and_4 (and_4_out, or_3_out, input_t_t_t_t_t);
  assign bit_extender_1_out = {{5{and_4_out}}, and_4_out};  // Bit_Extender bit_extender_1
  or or_1 (or_1_out, ~or_3_out, and_1_out);  // OR_Gate
  Demultiplexer #(.select(3)) demultiplexer_1 (
    .out0(input_t_t_t), .out1(input_t_t), .out2(input_plus), .out3(input_minus), .out4(stdout_ready),
    .out5(stdin_read), .out6(input_t_t_t_t), .out7(input_t_t_t_t_t), .in(or_1_out), .sel(instr));  // open: en
  Register24Stack64 register24stack64_1 (
    .clk(clk), .push(and_2_out), .insert_data(instr_ptr), .pop(and_3_out), .tail(register24stack64_1_tail),
    .err(err_stack), .length(dbg_stack_length));
  or or_2 (or_2_out, ~or_4_out, or_3_out);  // OR_Gate
  and and_5 (and_5_out, or_2_out, input_t_t_t_t);
  Adder #(.width(6)) adder_1 (
    .a(bit_extender_1_out), .b(dbg_skip_stack_size), .out(adder_1_out), .cin(and_5_out));  // open: cout
  or or_3 (or_3_out, dbg_skip_stack_size[5], dbg_skip_stack_size[4], dbg_skip_stack_size[3], dbg_skip_stack_size[2], dbg_skip_stack_size[1], dbg_skip_stack_size[0]);
  Register #(.width(6)) register_1 (.D(adder_1_out), .Q(dbg_skip_stack_size), .clk(clk));  // open: en, clr
  or or_4 (or_4_out, mem[0], mem[1], mem[2], mem[3], mem[4], mem[5], mem[6], mem[7]);
  assign bit_extender_2_out = {{23{input_t_t}}, input_t_t};  // Bit_Extender bit_extender_2
  assign bit_extender_3_out = {{7{input_minus}}, input_minus};  // Bit_Extender bit_extender_3
  // Probe on dbg_stack_length
  and and_6 (and_6_out, or_4_out, input_t_t_t_t_t);
  Adder #(.width(24)) adder_2 (.a(mem_ptr), .b(bit_extender_2_out), .out(mem_ptr_2), .cin(input_t_t_t));  // open: cout
  or or_5 (writing_mem, input_plus, input_minus, stdin_read);
  Adder adder_3 (.a(mem), .b(bit_extender_3_out), .out(adder_3_out), .cin(input_plus));  // open: cout
  Comparator #(.width(6)) comparator_1 (.a(dbg_stack_length), .b({6{1'b0}}), .eq(comparator_1_eq));  // open: gt, lt
  Multiplexer #(.width(24)) multiplexer_1 (
    .in0(instr_ptr), .in1(register24stack64_1_tail), .out(multiplexer_1_out), .sel(and_6_out));  // open: en
  Multiplexer #(.width(8)) multiplexer_2 (.in0(adder_3_out), .in1(stdin), .out(set_mem), .sel(stdin_read));  // open: en
  or or_6 (err, err_stack, and_7_out);
  and and_7 (and_7_out, comparator_1_eq, input_t_t_t_t_t);
  Adder #(.width(24)) adder_4 (.a(multiplexer_1_out), .b(24'h1), .out(instr_ptr_2));  // open: cin, cout

  assign stdout = mem;

  // Other names for the same wires on the sheet: input = stdin_read; input_t = stdout_ready;
  //   stack_length[5:0] = dbg_stack_length
endmodule

module output_stream (
  input  clk,
  input  probing,
  input  [23:0] probe_addr,
  input  writing,
  input  [7:0] value,
  output [7:0] probe_output
);

  wire [23:0] adder_1_out, multiplexer_1_out, register_1_q;

  Multiplexer #(.width(24)) multiplexer_1 (
    .in0(register_1_q), .in1(probe_addr), .out(multiplexer_1_out));  // open: sel, en
  Register #(.width(24)) register_1 (.D(adder_1_out), .Q(register_1_q), .clk(clk));  // open: en, clr
  Adder #(.width(24)) adder_1 (.a(register_1_q), .b({24{1'b0}}), .out(adder_1_out), .cin(writing));  // open: cout
  RAM #(.addrWidth(24), .bus("separate")) ram_1 (
    .addr(multiplexer_1_out), .din(value), .data(probe_output), .str(writing), .clk(clk), .ld(probing));  // open: sel, clr
endmodule

module input_stream (
  input  clk,
  input  read,
  output [7:0] out_3
);

  wire [23:0] adder_1_out, register_1_q;

  Adder #(.width(24)) adder_1 (.a(register_1_q), .b({24{1'b0}}), .out(adder_1_out), .cin(read));  // open: cout
  Register #(.width(24)) register_1 (.D(adder_1_out), .Q(register_1_q), .clk(clk));  // open: en, clr
  ROM #(.addrWidth(24)) rom_1 (.addr(register_1_q), .data(out_3));  // open: sel

  // Notes on the sheet:
  //   contents of rom_1 (hex, n*v repeats v):
  //   de ad c0 de ca fe f3 3d
endmodule

// Register24\nStack[64]
module Register24Stack64 (
  input  clk,
  input  push,
  input  pop,
  input  [23:0] insert_data,
  output [5:0] length,
  output [23:0] tail,
  output err
);

  wire and_1_out, not_1_out, not_2_out, not_3_out, or_1_out, stack_overflow_out, stack_underflow_out;
  wire [5:0] adder_1_out, bit_extender_1_out, subtractor_1_out;
  wire [23:0] multiplexer_1_out;

  not not_1 (not_1_out, push);
  Subtractor #(.width(6)) subtractor_1 (
    .a(length), .b({6{1'b0}}), .out(subtractor_1_out), .bin(not_1_out));  // open: bout
  Multiplexer #(.width(24)) multiplexer_1 (
    .in0({24{1'b0}}), .in1(insert_data), .out(multiplexer_1_out), .sel(push));  // open: en
  not not_2 (not_2_out, err);
  not not_3 (not_3_out, or_1_out);
  or or_1 (or_1_out, push, pop);
  Adder #(.width(6)) adder_1 (.a(length), .b(bit_extender_1_out), .out(adder_1_out), .cin(push));  // open: cout
  assign bit_extender_1_out = {{5{pop}}, pop};  // Bit_Extender bit_extender_1
  RAM #(.addrWidth(6), .dataWidth(24), .bus("separate")) ram_1 (
    .addr(subtractor_1_out), .din(multiplexer_1_out), .data(tail), .str(or_1_out), .sel(not_2_out),
    .clk(clk), .ld(not_3_out));  // open: clr
  Register #(.width(6)) u_length (.D(adder_1_out), .Q(length), .clk(clk));  // open: en, clr
  and stack_overflow (stack_overflow_out, length[0], length[1], length[2], length[3], length[4], length[5], push);
  and and_1 (and_1_out, push, pop);
  and stack_underflow (stack_underflow_out, ~length[0], ~length[1], ~length[2], ~length[3], ~length[4], ~length[5], pop);  // AND_Gate
  or or_2 (err, stack_overflow_out, and_1_out, stack_underflow_out);
endmodule
